// Logisim project screen.circ as structural Verilog: 3 circuits, main circuit main
module main (
);

  wire clock_1_out, comparator_1_eq, demultiplexer_1_out0, demultiplexer_1_out1, demultiplexer_1_out2,
       demultiplexer_1_out3, demultiplexer_1_out4, demultiplexer_1_out5, demultiplexer_1_out6,
       demultiplexer_1_out7, demultiplexer_1_out8, demultiplexer_1_out9, demultiplexer_1_out10,
       demultiplexer_1_out11, demultiplexer_1_out12, demultiplexer_1_out13, demultiplexer_1_out14,
       demultiplexer_1_out15, demultiplexer_1_out16, demultiplexer_1_out17, demultiplexer_1_out18,
       demultiplexer_1_out19, demultiplexer_1_out20, demultiplexer_1_out21, demultiplexer_1_out22,
       demultiplexer_1_out23, demultiplexer_1_out24, demultiplexer_1_out25, demultiplexer_1_out26,
       demultiplexer_1_out27, demultiplexer_1_out28, demultiplexer_1_out29, demultiplexer_1_out30,
       demultiplexer_1_out31, demultiplexer_2_out0, demultiplexer_2_out1, demultiplexer_2_out2,
       demultiplexer_2_out3, demultiplexer_2_out4, demultiplexer_2_out5, demultiplexer_2_out6,
       demultiplexer_2_out7, demultiplexer_2_out8, demultiplexer_2_out9, demultiplexer_2_out10,
       demultiplexer_2_out11, demultiplexer_2_out12, demultiplexer_2_out13, demultiplexer_2_out14,
       demultiplexer_2_out15, demultiplexer_2_out16, demultiplexer_2_out17, demultiplexer_2_out18,
       demultiplexer_2_out19, demultiplexer_2_out20, demultiplexer_2_out21, demultiplexer_2_out22,
       demultiplexer_2_out23, demultiplexer_2_out24, demultiplexer_2_out25, demultiplexer_2_out26,
       demultiplexer_2_out27, demultiplexer_2_out28, demultiplexer_2_out29, demultiplexer_2_out30,
       demultiplexer_2_out31, demultiplexer_3_out0, demultiplexer_3_out1, demultiplexer_3_out2,
       demultiplexer_3_out3, demultiplexer_3_out4, demultiplexer_3_out5, demultiplexer_3_out6,
       demultiplexer_3_out7, demultiplexer_3_out8, demultiplexer_3_out9, demultiplexer_3_out10,
       demultiplexer_3_out11, demultiplexer_3_out12, demultiplexer_3_out13, demultiplexer_3_out14,
       demultiplexer_3_out15, demultiplexer_3_out16, demultiplexer_3_out17, demultiplexer_3_out18,
       demultiplexer_3_out19, demultiplexer_3_out20, demultiplexer_3_out21, demultiplexer_3_out22,
       demultiplexer_3_out23, demultiplexer_3_out24, demultiplexer_3_out25, demultiplexer_3_out26,
       demultiplexer_3_out27, demultiplexer_3_out28, demultiplexer_3_out29, demultiplexer_3_out30,
       demultiplexer_3_out31, demultiplexer_4_out0, demultiplexer_4_out1, demultiplexer_4_out2,
       demultiplexer_4_out3, demultiplexer_4_out4, demultiplexer_4_out5, demultiplexer_4_out6,
       demultiplexer_4_out7, demultiplexer_4_out8, demultiplexer_4_out9, demultiplexer_4_out10,
       demultiplexer_4_out11, demultiplexer_4_out12, demultiplexer_4_out13, demultiplexer_4_out14,
       demultiplexer_4_out15, demultiplexer_4_out16, demultiplexer_4_out17, demultiplexer_4_out18,
       demultiplexer_4_out19, demultiplexer_4_out20, demultiplexer_4_out21, demultiplexer_4_out22,
       demultiplexer_4_out23, demultiplexer_4_out24, demultiplexer_4_out25, demultiplexer_4_out26,
       demultiplexer_4_out27, demultiplexer_4_out28, demultiplexer_4_out29, demultiplexer_4_out30,
       demultiplexer_4_out31, not_1_out;
  wire [4:0] Row_q;
  wire [19:0] Address_q;
  wire [31:0] counter_1_q, pixelmem2_1_pixelout, pixelmem2_2_pixelout, pixelmem2_3_pixelout,
       pixelmem2_4_pixelout, pixelmem2_5_pixelout, pixelmem2_6_pixelout, pixelmem2_7_pixelout,
       pixelmem2_8_pixelout, pixelmem2_9_pixelout, pixelmem2_10_pixelout, pixelmem2_11_pixelout,
       pixelmem2_12_pixelout, pixelmem2_13_pixelout, pixelmem2_14_pixelout, pixelmem2_15_pixelout,
       pixelmem2_16_pixelout, pixelmem2_17_pixelout, pixelmem2_18_pixelout, pixelmem2_19_pixelout,
       pixelmem2_20_pixelout, pixelmem2_21_pixelout, pixelmem2_22_pixelout, pixelmem2_23_pixelout,
       pixelmem2_24_pixelout, pixelmem2_25_pixelout, pixelmem2_26_pixelout, pixelmem2_27_pixelout,
       pixelmem2_28_pixelout, pixelmem2_29_pixelout, pixelmem2_30_pixelout, pixelmem2_31_pixelout,
       pixelmem2_32_pixelout, pixelmem2_33_pixelout, pixelmem2_34_pixelout, pixelmem2_35_pixelout,
       pixelmem2_36_pixelout, pixelmem2_37_pixelout, pixelmem2_38_pixelout, pixelmem2_39_pixelout,
       pixelmem2_40_pixelout, pixelmem2_41_pixelout, pixelmem2_42_pixelout, pixelmem2_43_pixelout,
       pixelmem2_44_pixelout, pixelmem2_45_pixelout, pixelmem2_46_pixelout, pixelmem2_47_pixelout,
       pixelmem2_48_pixelout, pixelmem2_49_pixelout, pixelmem2_50_pixelout, pixelmem2_51_pixelout,
       pixelmem2_52_pixelout, pixelmem2_53_pixelout, pixelmem2_54_pixelout, pixelmem2_55_pixelout,
       pixelmem2_56_pixelout, pixelmem2_57_pixelout, pixelmem2_58_pixelout, pixelmem2_59_pixelout,
       pixelmem2_60_pixelout, pixelmem2_61_pixelout, pixelmem2_62_pixelout, pixelmem2_63_pixelout,
       pixelmem2_64_pixelout, pixelmem_1_pixelout, pixelmem_2_pixelout, pixelmem_3_pixelout,
       pixelmem_4_pixelout, pixelmem_5_pixelout, pixelmem_6_pixelout, pixelmem_7_pixelout,
       pixelmem_8_pixelout, pixelmem_9_pixelout, pixelmem_10_pixelout, pixelmem_11_pixelout,
       pixelmem_12_pixelout, pixelmem_13_pixelout, pixelmem_14_pixelout, pixelmem_15_pixelout,
       pixelmem_16_pixelout, pixelmem_17_pixelout, pixelmem_18_pixelout, pixelmem_19_pixelout,
       pixelmem_20_pixelout, pixelmem_21_pixelout, pixelmem_22_pixelout, pixelmem_23_pixelout,
       pixelmem_24_pixelout, pixelmem_25_pixelout, pixelmem_26_pixelout, pixelmem_27_pixelout,
       pixelmem_28_pixelout, pixelmem_29_pixelout, pixelmem_30_pixelout, pixelmem_31_pixelout,
       pixelmem_32_pixelout, pixelmem_33_pixelout, pixelmem_34_pixelout, pixelmem_35_pixelout,
       pixelmem_36_pixelout, pixelmem_37_pixelout, pixelmem_38_pixelout, pixelmem_39_pixelout,
       pixelmem_40_pixelout, pixelmem_41_pixelout, pixelmem_42_pixelout, pixelmem_43_pixelout,
       pixelmem_44_pixelout, pixelmem_45_pixelout, pixelmem_46_pixelout, pixelmem_47_pixelout,
       pixelmem_48_pixelout, pixelmem_49_pixelout, pixelmem_50_pixelout, pixelmem_51_pixelout,
       pixelmem_52_pixelout, pixelmem_53_pixelout, pixelmem_54_pixelout, pixelmem_55_pixelout,
       pixelmem_56_pixelout, pixelmem_57_pixelout, pixelmem_58_pixelout, pixelmem_59_pixelout,
       pixelmem_60_pixelout, pixelmem_61_pixelout, pixelmem_62_pixelout, pixelmem_63_pixelout,
       pixelmem_64_pixelout, rom_1_data, rom_2_data, rom_3_data, rom_4_data;

  ROM #(.addrWidth(20), .dataWidth(32)) rom_1 (.addr(Address_q), .data(rom_1_data));  // open: sel
  ROM #(.addrWidth(20), .dataWidth(32)) rom_2 (.addr(Address_q), .data(rom_2_data));  // open: sel
  Demultiplexer #(.select(5)) demultiplexer_1 (
    .out0(demultiplexer_1_out0), .out1(demultiplexer_1_out1), .out2(demultiplexer_1_out2),
    .out3(demultiplexer_1_out3), .out4(demultiplexer_1_out4), .out5(demultiplexer_1_out5),
    .out6(demultiplexer_1_out6), .out7(demultiplexer_1_out7), .out8(demultiplexer_1_out8),
    .out9(demultiplexer_1_out9), .out10(demultiplexer_1_out10), .out11(demultiplexer_1_out11),
    .out12(demultiplexer_1_out12), .out13(demultiplexer_1_out13), .out14(demultiplexer_1_out14),
    .out15(demultiplexer_1_out15), .out16(demultiplexer_1_out16), .out17(demultiplexer_1_out17),
    .out18(demultiplexer_1_out18), .out19(demultiplexer_1_out19), .out20(demultiplexer_1_out20),
    .out21(demultiplexer_1_out21), .out22(demultiplexer_1_out22), .out23(demultiplexer_1_out23),
    .out24(demultiplexer_1_out24), .out25(demultiplexer_1_out25), .out26(demultiplexer_1_out26),
    .out27(demultiplexer_1_out27), .out28(demultiplexer_1_out28), .out29(demultiplexer_1_out29),
    .out30(demultiplexer_1_out30), .out31(demultiplexer_1_out31), .in(not_1_out), .sel(Row_q));  // open: en
  Demultiplexer #(.select(5)) demultiplexer_2 (
    .out0(demultiplexer_2_out0), .out1(demultiplexer_2_out1), .out2(demultiplexer_2_out2),
    .out3(demultiplexer_2_out3), .out4(demultiplexer_2_out4), .out5(demultiplexer_2_out5),
    .out6(demultiplexer_2_out6), .out7(demultiplexer_2_out7), .out8(demultiplexer_2_out8),
    .out9(demultiplexer_2_out9), .out10(demultiplexer_2_out10), .out11(demultiplexer_2_out11),
    .out12(demultiplexer_2_out12), .out13(demultiplexer_2_out13), .out14(demultiplexer_2_out14),
    .out15(demultiplexer_2_out15), .out16(demultiplexer_2_out16), .out17(demultiplexer_2_out17),
    .out18(demultiplexer_2_out18), .out19(demultiplexer_2_out19), .out20(demultiplexer_2_out20),
    .out21(demultiplexer_2_out21), .out22(demultiplexer_2_out22), .out23(demultiplexer_2_out23),
    .out24(demultiplexer_2_out24), .out25(demultiplexer_2_out25), .out26(demultiplexer_2_out26),
    .out27(demultiplexer_2_out27), .out28(demultiplexer_2_out28), .out29(demultiplexer_2_out29),
    .out30(demultiplexer_2_out30), .out31(demultiplexer_2_out31), .in(not_1_out), .sel(Row_q));  // open: en
  Clock clock_1 (.out(clock_1_out));
  pixelmem pixelmem_1 (
    .Data(rom_1_data), .Store(demultiplexer_1_out0), .PixelOut(pixelmem_1_pixelout), .Draw(comparator_1_eq));
  pixelmem pixelmem_2 (
    .Data(rom_1_data), .Store(demultiplexer_1_out1), .PixelOut(pixelmem_2_pixelout), .Draw(comparator_1_eq));
  DotMatrix #(.inputtype("row"), .matrixcols(32), .matrixrows(32), .persist(1)) dotmatrix_1 (
    .row0(pixelmem_1_pixelout), .row1(pixelmem_2_pixelout), .row2(pixelmem_3_pixelout),
    .row3(pixelmem_4_pixelout), .row4(pixelmem_5_pixelout), .row5(pixelmem_6_pixelout),
    .row6(pixelmem_7_pixelout), .row7(pixelmem_8_pixelout), .row8(pixelmem_9_pixelout),
    .row9(pixelmem_10_pixelout), .row10(pixelmem_11_pixelout), .row11(pixelmem_12_pixelout),
    .row12(pixelmem_13_pixelout), .row13(pixelmem_14_pixelout), .row14(pixelmem_15_pixelout),
    .row15(pixelmem_16_pixelout), .row16(pixelmem_17_pixelout), .row17(pixelmem_18_pixelout),
    .row18(pixelmem_19_pixelout), .row19(pixelmem_20_pixelout), .row20(pixelmem_21_pixelout),
    .row21(pixelmem_22_pixelout), .row22(pixelmem_23_pixelout), .row23(pixelmem_24_pixelout),
    .row24(pixelmem_25_pixelout), .row25(pixelmem_26_pixelout), .row26(pixelmem_27_pixelout),
    .row27(pixelmem_28_pixelout), .row28(pixelmem_29_pixelout), .row29(pixelmem_30_pixelout),
    .row30(pixelmem_31_pixelout), .row31(pixelmem_32_pixelout));
  pixelmem pixelmem_3 (
    .Data(rom_1_data), .Store(demultiplexer_1_out2), .PixelOut(pixelmem_3_pixelout), .Draw(comparator_1_eq));
  pixelmem pixelmem_4 (
    .Data(rom_1_data), .Store(demultiplexer_1_out3), .PixelOut(pixelmem_4_pixelout), .Draw(comparator_1_eq));
  pixelmem pixelmem_5 (
    .Data(rom_1_data), .Store(demultiplexer_1_out4), .PixelOut(pixelmem_5_pixelout), .Draw(comparator_1_eq));
  pixelmem pixelmem_6 (
    .Data(rom_1_data), .Store(demultiplexer_1_out5), .PixelOut(pixelmem_6_pixelout), .Draw(comparator_1_eq));
  pixelmem pixelmem_7 (
    .Data(rom_1_data), .Store(demultiplexer_1_out6), .PixelOut(pixelmem_7_pixelout), .Draw(comparator_1_eq));
  pixelmem pixelmem_8 (
    .Data(rom_1_data), .Store(demultiplexer_1_out7), .PixelOut(pixelmem_8_pixelout), .Draw(comparator_1_eq));
  pixelmem pixelmem_9 (
    .Data(rom_1_data), .Store(demultiplexer_1_out8), .PixelOut(pixelmem_9_pixelout), .Draw(comparator_1_eq));
  pixelmem pixelmem_10 (
    .Data(rom_1_data), .Store(demultiplexer_1_out9), .PixelOut(pixelmem_10_pixelout), .Draw(comparator_1_eq));
  pixelmem pixelmem_11 (
    .Data(rom_1_data), .Store(demultiplexer_1_out10), .PixelOut(pixelmem_11_pixelout), .Draw(comparator_1_eq));
  pixelmem pixelmem_12 (
    .Data(rom_1_data), .Store(demultiplexer_1_out11), .PixelOut(pixelmem_12_pixelout), .Draw(comparator_1_eq));
  pixelmem pixelmem_13 (
    .Data(rom_1_data), .Store(demultiplexer_1_out12), .PixelOut(pixelmem_13_pixelout), .Draw(comparator_1_eq));
  pixelmem pixelmem_14 (
    .Data(rom_1_data), .Store(demultiplexer_1_out13), .PixelOut(pixelmem_14_pixelout), .Draw(comparator_1_eq));
  pixelmem pixelmem_15 (
    .Data(rom_1_data), .Store(demultiplexer_1_out14), .PixelOut(pixelmem_15_pixelout), .Draw(comparator_1_eq));
  pixelmem pixelmem_16 (
    .Data(rom_1_data), .Store(demultiplexer_1_out15), .PixelOut(pixelmem_16_pixelout), .Draw(comparator_1_eq));
  pixelmem pixelmem_17 (
    .Data(rom_1_data), .Store(demultiplexer_1_out16), .PixelOut(pixelmem_17_pixelout), .Draw(comparator_1_eq));
  pixelmem pixelmem_18 (
    .Data(rom_1_data), .Store(demultiplexer_1_out17), .PixelOut(pixelmem_18_pixelout), .Draw(comparator_1_eq));
  pixelmem pixelmem_19 (
    .Data(rom_1_data), .Store(demultiplexer_1_out18), .PixelOut(pixelmem_19_pixelout), .Draw(comparator_1_eq));
  pixelmem pixelmem_20 (
    .Data(rom_1_data), .Store(demultiplexer_1_out19), .PixelOut(pixelmem_20_pixelout), .Draw(comparator_1_eq));
  pixelmem pixelmem_21 (
    .Data(rom_1_data), .Store(demultiplexer_1_out20), .PixelOut(pixelmem_21_pixelout), .Draw(comparator_1_eq));
  pixelmem pixelmem_22 (
    .Data(rom_1_data), .Store(demultiplexer_1_out21), .PixelOut(pixelmem_22_pixelout), .Draw(comparator_1_eq));
  pixelmem pixelmem_23 (
    .Data(rom_1_data), .Store(demultiplexer_1_out22), .PixelOut(pixelmem_23_pixelout), .Draw(comparator_1_eq));
  pixelmem pixelmem_24 (
    .Data(rom_1_data), .Store(demultiplexer_1_out23), .PixelOut(pixelmem_24_pixelout), .Draw(comparator_1_eq));
  pixelmem pixelmem_25 (
    .Data(rom_1_data), .Store(demultiplexer_1_out24), .PixelOut(pixelmem_25_pixelout), .Draw(comparator_1_eq));
  pixelmem pixelmem_26 (
    .Data(rom_1_data), .Store(demultiplexer_1_out25), .PixelOut(pixelmem_26_pixelout), .Draw(comparator_1_eq));
  pixelmem pixelmem_27 (
    .Data(rom_1_data), .Store(demultiplexer_1_out26), .PixelOut(pixelmem_27_pixelout), .Draw(comparator_1_eq));
  pixelmem pixelmem_28 (
    .Data(rom_1_data), .Store(demultiplexer_1_out27), .PixelOut(pixelmem_28_pixelout), .Draw(comparator_1_eq));
  pixelmem pixelmem_29 (
    .Data(rom_1_data), .Store(demultiplexer_1_out28), .PixelOut(pixelmem_29_pixelout), .Draw(comparator_1_eq));
  pixelmem pixelmem_30 (
    .Data(rom_1_data), .Store(demultiplexer_1_out29), .PixelOut(pixelmem_30_pixelout), .Draw(comparator_1_eq));
  pixelmem pixelmem_31 (
    .Data(rom_1_data), .Store(demultiplexer_1_out30), .PixelOut(pixelmem_31_pixelout), .Draw(comparator_1_eq));
  pixelmem pixelmem_32 (
    .Data(rom_1_data), .Store(demultiplexer_1_out31), .PixelOut(pixelmem_32_pixelout), .Draw(comparator_1_eq));
  pixelmem2 pixelmem2_1 (
    .Data(rom_2_data), .PixelOut(pixelmem2_1_pixelout), .Store(demultiplexer_2_out0), .Draw(comparator_1_eq));
  DotMatrix #(.inputtype("row"), .matrixcols(32), .matrixrows(32), .persist(1)) dotmatrix_2 (
    .row0(pixelmem2_1_pixelout), .row1(pixelmem2_2_pixelout), .row2(pixelmem2_3_pixelout),
    .row3(pixelmem2_4_pixelout), .row4(pixelmem2_5_pixelout), .row5(pixelmem2_6_pixelout),
    .row6(pixelmem2_7_pixelout), .row7(pixelmem2_8_pixelout), .row8(pixelmem2_9_pixelout),
    .row9(pixelmem2_10_pixelout), .row10(pixelmem2_11_pixelout), .row11(pixelmem2_12_pixelout),
    .row12(pixelmem2_13_pixelout), .row13(pixelmem2_14_pixelout), .row14(pixelmem2_15_pixelout),
    .row15(pixelmem2_16_pixelout), .row16(pixelmem2_17_pixelout), .row17(pixelmem2_18_pixelout),
    .row18(pixelmem2_19_pixelout), .row19(pixelmem2_20_pixelout), .row20(pixelmem2_21_pixelout),
    .row21(pixelmem2_22_pixelout), .row22(pixelmem2_23_pixelout), .row23(pixelmem2_24_pixelout),
    .row24(pixelmem2_25_pixelout), .row25(pixelmem2_26_pixelout), .row26(pixelmem2_27_pixelout),
    .row27(pixelmem2_28_pixelout), .row28(pixelmem2_29_pixelout), .row29(pixelmem2_30_pixelout),
    .row30(pixelmem2_31_pixelout), .row31(pixelmem2_32_pixelout));
  pixelmem2 pixelmem2_2 (
    .Data(rom_2_data), .PixelOut(pixelmem2_2_pixelout), .Store(demultiplexer_2_out1), .Draw(comparator_1_eq));
  pixelmem2 pixelmem2_3 (
    .Data(rom_2_data), .PixelOut(pixelmem2_3_pixelout), .Store(demultiplexer_2_out2), .Draw(comparator_1_eq));
  pixelmem2 pixelmem2_4 (
    .Data(rom_2_data), .PixelOut(pixelmem2_4_pixelout), .Store(demultiplexer_2_out3), .Draw(comparator_1_eq));
  pixelmem2 pixelmem2_5 (
    .Data(rom_2_data), .PixelOut(pixelmem2_5_pixelout), .Store(demultiplexer_2_out4), .Draw(comparator_1_eq));
  pixelmem2 pixelmem2_6 (
    .Data(rom_2_data), .PixelOut(pixelmem2_6_pixelout), .Store(demultiplexer_2_out5), .Draw(comparator_1_eq));
  pixelmem2 pixelmem2_7 (
    .Data(rom_2_data), .PixelOut(pixelmem2_7_pixelout), .Store(demultiplexer_2_out6), .Draw(comparator_1_eq));
  pixelmem2 pixelmem2_8 (
    .Data(rom_2_data), .PixelOut(pixelmem2_8_pixelout), .Store(demultiplexer_2_out7), .Draw(comparator_1_eq));
  pixelmem2 pixelmem2_9 (
    .Data(rom_2_data), .PixelOut(pixelmem2_9_pixelout), .Store(demultiplexer_2_out8), .Draw(comparator_1_eq));
  pixelmem2 pixelmem2_10 (
    .Data(rom_2_data), .PixelOut(pixelmem2_10_pixelout), .Store(demultiplexer_2_out9), .Draw(comparator_1_eq));
  pixelmem2 pixelmem2_11 (
    .Data(rom_2_data), .PixelOut(pixelmem2_11_pixelout), .Store(demultiplexer_2_out10), .Draw(comparator_1_eq));
  pixelmem2 pixelmem2_12 (
    .Data(rom_2_data), .PixelOut(pixelmem2_12_pixelout), .Store(demultiplexer_2_out11), .Draw(comparator_1_eq));
  pixelmem2 pixelmem2_13 (
    .Data(rom_2_data), .PixelOut(pixelmem2_13_pixelout), .Store(demultiplexer_2_out12), .Draw(comparator_1_eq));
  pixelmem2 pixelmem2_14 (
    .Data(rom_2_data), .PixelOut(pixelmem2_14_pixelout), .Store(demultiplexer_2_out13), .Draw(comparator_1_eq));
  pixelmem2 pixelmem2_15 (
    .Data(rom_2_data), .PixelOut(pixelmem2_15_pixelout), .Store(demultiplexer_2_out14), .Draw(comparator_1_eq));
  pixelmem2 pixelmem2_16 (
    .Data(rom_2_data), .PixelOut(pixelmem2_16_pixelout), .Store(demultiplexer_2_out15), .Draw(comparator_1_eq));
  pixelmem2 pixelmem2_17 (
    .Data(rom_2_data), .PixelOut(pixelmem2_17_pixelout), .Store(demultiplexer_2_out16), .Draw(comparator_1_eq));
  pixelmem2 pixelmem2_18 (
    .Data(rom_2_data), .PixelOut(pixelmem2_18_pixelout), .Store(demultiplexer_2_out17), .Draw(comparator_1_eq));
  pixelmem2 pixelmem2_19 (
    .Data(rom_2_data), .PixelOut(pixelmem2_19_pixelout), .Store(demultiplexer_2_out18), .Draw(comparator_1_eq));
  pixelmem2 pixelmem2_20 (
    .Data(rom_2_data), .PixelOut(pixelmem2_20_pixelout), .Store(demultiplexer_2_out19), .Draw(comparator_1_eq));
  pixelmem2 pixelmem2_21 (
    .Data(rom_2_data), .PixelOut(pixelmem2_21_pixelout), .Store(demultiplexer_2_out20), .Draw(comparator_1_eq));
  pixelmem2 pixelmem2_22 (
    .Data(rom_2_data), .PixelOut(pixelmem2_22_pixelout), .Store(demultiplexer_2_out21), .Draw(comparator_1_eq));
  pixelmem2 pixelmem2_23 (
    .Data(rom_2_data), .PixelOut(pixelmem2_23_pixelout), .Store(demultiplexer_2_out22), .Draw(comparator_1_eq));
  pixelmem2 pixelmem2_24 (
    .Data(rom_2_data), .PixelOut(pixelmem2_24_pixelout), .Store(demultiplexer_2_out23), .Draw(comparator_1_eq));
  pixelmem2 pixelmem2_25 (
    .Data(rom_2_data), .PixelOut(pixelmem2_25_pixelout), .Store(demultiplexer_2_out24), .Draw(comparator_1_eq));
  pixelmem2 pixelmem2_26 (
    .Data(rom_2_data), .PixelOut(pixelmem2_26_pixelout), .Store(demultiplexer_2_out25), .Draw(comparator_1_eq));
  pixelmem2 pixelmem2_27 (
    .Data(rom_2_data), .PixelOut(pixelmem2_27_pixelout), .Store(demultiplexer_2_out26), .Draw(comparator_1_eq));
  pixelmem2 pixelmem2_28 (
    .Data(rom_2_data), .PixelOut(pixelmem2_28_pixelout), .Store(demultiplexer_2_out27), .Draw(comparator_1_eq));
  pixelmem2 pixelmem2_29 (
    .Data(rom_2_data), .PixelOut(pixelmem2_29_pixelout), .Store(demultiplexer_2_out28), .Draw(comparator_1_eq));
  pixelmem2 pixelmem2_30 (
    .Data(rom_2_data), .PixelOut(pixelmem2_30_pixelout), .Store(demultiplexer_2_out29), .Draw(comparator_1_eq));
  pixelmem2 pixelmem2_31 (
    .Data(rom_2_data), .PixelOut(pixelmem2_31_pixelout), .Store(demultiplexer_2_out30), .Draw(comparator_1_eq));
  pixelmem2 pixelmem2_32 (
    .Data(rom_2_data), .PixelOut(pixelmem2_32_pixelout), .Store(demultiplexer_2_out31), .Draw(comparator_1_eq));
  not not_1 (not_1_out, clock_1_out);
  Counter #(.width(20), .max('hfffff)) Address (.Q(Address_q), .clk(clock_1_out));  // open: load, D, count, carry, clr
  DotMatrix #(.inputtype("row"), .matrixcols(32), .matrixrows(32), .persist(1)) dotmatrix_3 (
    .row0(pixelmem2_33_pixelout), .row1(pixelmem2_34_pixelout), .row2(pixelmem2_35_pixelout),
    .row3(pixelmem2_36_pixelout), .row4(pixelmem2_37_pixelout), .row5(pixelmem2_38_pixelout),
    .row6(pixelmem2_39_pixelout), .row7(pixelmem2_40_pixelout), .row8(pixelmem2_41_pixelout),
    .row9(pixelmem2_42_pixelout), .row10(pixelmem2_43_pixelout), .row11(pixelmem2_44_pixelout),
    .row12(pixelmem2_45_pixelout), .row13(pixelmem2_46_pixelout), .row14(pixelmem2_47_pixelout),
    .row15(pixelmem2_48_pixelout), .row16(pixelmem2_49_pixelout), .row17(pixelmem2_50_pixelout),
    .row18(pixelmem2_51_pixelout), .row19(pixelmem2_52_pixelout), .row20(pixelmem2_53_pixelout),
    .row21(pixelmem2_54_pixelout), .row22(pixelmem2_55_pixelout), .row23(pixelmem2_56_pixelout),
    .row24(pixelmem2_57_pixelout), .row25(pixelmem2_58_pixelout), .row26(pixelmem2_59_pixelout),
    .row27(pixelmem2_60_pixelout), .row28(pixelmem2_61_pixelout), .row29(pixelmem2_62_pixelout),
    .row30(pixelmem2_63_pixelout), .row31(pixelmem2_64_pixelout));
  DotMatrix #(.inputtype("row"), .matrixcols(32), .matrixrows(32), .persist(1)) dotmatrix_4 (
    .row0(pixelmem_33_pixelout), .row1(pixelmem_34_pixelout), .row2(pixelmem_35_pixelout),
    .row3(pixelmem_36_pixelout), .row4(pixelmem_37_pixelout), .row5(pixelmem_38_pixelout),
    .row6(pixelmem_39_pixelout), .row7(pixelmem_40_pixelout), .row8(pixelmem_41_pixelout),
    .row9(pixelmem_42_pixelout), .row10(pixelmem_43_pixelout), .row11(pixelmem_44_pixelout),
    .row12(pixelmem_45_pixelout), .row13(pixelmem_46_pixelout), .row14(pixelmem_47_pixelout),
    .row15(pixelmem_48_pixelout), .row16(pixelmem_49_pixelout), .row17(pixelmem_50_pixelout),
    .row18(pixelmem_51_pixelout), .row19(pixelmem_52_pixelout), .row20(pixelmem_53_pixelout),
    .row21(pixelmem_54_pixelout), .row22(pixelmem_55_pixelout), .row23(pixelmem_56_pixelout),
    .row24(pixelmem_57_pixelout), .row25(pixelmem_58_pixelout), .row26(pixelmem_59_pixelout),
    .row27(pixelmem_60_pixelout), .row28(pixelmem_61_pixelout), .row29(pixelmem_62_pixelout),
    .row30(pixelmem_63_pixelout), .row31(pixelmem_64_pixelout));
  Counter #(.width(5), .max('h1f)) Row (.Q(Row_q), .clk(clock_1_out));  // open: load, D, count, carry, clr
  Comparator #(.width(5), .mode("unsigned")) comparator_1 (
    .a(Row_q), .b({5{1'b0}}), .eq(comparator_1_eq));  // open: gt, lt
  Counter #(.width(32), .max('hffffffff)) counter_1 (
    .Q(counter_1_q), .clk(comparator_1_eq));  // open: load, D, count, carry, clr
  // Probe on counter_1_q
  pixelmem2 pixelmem2_33 (
    .Data(rom_3_data), .PixelOut(pixelmem2_33_pixelout), .Store(demultiplexer_3_out0), .Draw(comparator_1_eq));
  pixelmem2 pixelmem2_34 (
    .Data(rom_3_data), .PixelOut(pixelmem2_34_pixelout), .Store(demultiplexer_3_out1), .Draw(comparator_1_eq));
  pixelmem2 pixelmem2_35 (
    .Data(rom_3_data), .PixelOut(pixelmem2_35_pixelout), .Store(demultiplexer_3_out2), .Draw(comparator_1_eq));
  pixelmem2 pixelmem2_36 (
    .Data(rom_3_data), .PixelOut(pixelmem2_36_pixelout), .Store(demultiplexer_3_out3), .Draw(comparator_1_eq));
  pixelmem2 pixelmem2_37 (
    .Data(rom_3_data), .PixelOut(pixelmem2_37_pixelout), .Store(demultiplexer_3_out4), .Draw(comparator_1_eq));
  pixelmem2 pixelmem2_38 (
    .Data(rom_3_data), .PixelOut(pixelmem2_38_pixelout), .Store(demultiplexer_3_out5), .Draw(comparator_1_eq));
  pixelmem2 pixelmem2_39 (
    .Data(rom_3_data), .PixelOut(pixelmem2_39_pixelout), .Store(demultiplexer_3_out6), .Draw(comparator_1_eq));
  pixelmem2 pixelmem2_40 (
    .Data(rom_3_data), .PixelOut(pixelmem2_40_pixelout), .Store(demultiplexer_3_out7), .Draw(comparator_1_eq));
  pixelmem2 pixelmem2_41 (
    .Data(rom_3_data), .PixelOut(pixelmem2_41_pixelout), .Store(demultiplexer_3_out8), .Draw(comparator_1_eq));
  pixelmem2 pixelmem2_42 (
    .Data(rom_3_data), .PixelOut(pixelmem2_42_pixelout), .Store(demultiplexer_3_out9), .Draw(comparator_1_eq));
  pixelmem2 pixelmem2_43 (
    .Data(rom_3_data), .PixelOut(pixelmem2_43_pixelout), .Store(demultiplexer_3_out10), .Draw(comparator_1_eq));
  pixelmem2 pixelmem2_44 (
    .Data(rom_3_data), .PixelOut(pixelmem2_44_pixelout), .Store(demultiplexer_3_out11), .Draw(comparator_1_eq));
  pixelmem2 pixelmem2_45 (
    .Data(rom_3_data), .PixelOut(pixelmem2_45_pixelout), .Store(demultiplexer_3_out12), .Draw(comparator_1_eq));
  pixelmem2 pixelmem2_46 (
    .Data(rom_3_data), .PixelOut(pixelmem2_46_pixelout), .Store(demultiplexer_3_out13), .Draw(comparator_1_eq));
  pixelmem2 pixelmem2_47 (
    .Data(rom_3_data), .PixelOut(pixelmem2_47_pixelout), .Store(demultiplexer_3_out14), .Draw(comparator_1_eq));
  pixelmem2 pixelmem2_48 (
    .Data(rom_3_data), .PixelOut(pixelmem2_48_pixelout), .Store(demultiplexer_3_out15), .Draw(comparator_1_eq));
  pixelmem2 pixelmem2_49 (
    .Data(rom_3_data), .PixelOut(pixelmem2_49_pixelout), .Store(demultiplexer_3_out16), .Draw(comparator_1_eq));
  pixelmem2 pixelmem2_50 (
    .Data(rom_3_data), .PixelOut(pixelmem2_50_pixelout), .Store(demultiplexer_3_out17), .Draw(comparator_1_eq));
  pixelmem2 pixelmem2_51 (
    .Data(rom_3_data), .PixelOut(pixelmem2_51_pixelout), .Store(demultiplexer_3_out18), .Draw(comparator_1_eq));
  pixelmem2 pixelmem2_52 (
    .Data(rom_3_data), .PixelOut(pixelmem2_52_pixelout), .Store(demultiplexer_3_out19), .Draw(comparator_1_eq));
  pixelmem2 pixelmem2_53 (
    .Data(rom_3_data), .PixelOut(pixelmem2_53_pixelout), .Store(demultiplexer_3_out20), .Draw(comparator_1_eq));
  pixelmem2 pixelmem2_54 (
    .Data(rom_3_data), .PixelOut(pixelmem2_54_pixelout), .Store(demultiplexer_3_out21), .Draw(comparator_1_eq));
  pixelmem2 pixelmem2_55 (
    .Data(rom_3_data), .PixelOut(pixelmem2_55_pixelout), .Store(demultiplexer_3_out22), .Draw(comparator_1_eq));
  pixelmem2 pixelmem2_56 (
    .Data(rom_3_data), .PixelOut(pixelmem2_56_pixelout), .Store(demultiplexer_3_out23), .Draw(comparator_1_eq));
  pixelmem2 pixelmem2_57 (
    .Data(rom_3_data), .PixelOut(pixelmem2_57_pixelout), .Store(demultiplexer_3_out24), .Draw(comparator_1_eq));
  pixelmem2 pixelmem2_58 (
    .Data(rom_3_data), .PixelOut(pixelmem2_58_pixelout), .Store(demultiplexer_3_out25), .Draw(comparator_1_eq));
  pixelmem2 pixelmem2_59 (
    .Data(rom_3_data), .PixelOut(pixelmem2_59_pixelout), .Store(demultiplexer_3_out26), .Draw(comparator_1_eq));
  pixelmem2 pixelmem2_60 (
    .Data(rom_3_data), .PixelOut(pixelmem2_60_pixelout), .Store(demultiplexer_3_out27), .Draw(comparator_1_eq));
  pixelmem2 pixelmem2_61 (
    .Data(rom_3_data), .PixelOut(pixelmem2_61_pixelout), .Store(demultiplexer_3_out28), .Draw(comparator_1_eq));
  pixelmem2 pixelmem2_62 (
    .Data(rom_3_data), .PixelOut(pixelmem2_62_pixelout), .Store(demultiplexer_3_out29), .Draw(comparator_1_eq));
  pixelmem2 pixelmem2_63 (
    .Data(rom_3_data), .PixelOut(pixelmem2_63_pixelout), .Store(demultiplexer_3_out30), .Draw(comparator_1_eq));
  pixelmem2 pixelmem2_64 (
    .Data(rom_3_data), .PixelOut(pixelmem2_64_pixelout), .Store(demultiplexer_3_out31), .Draw(comparator_1_eq));
  pixelmem pixelmem_33 (
    .Data(rom_4_data), .Store(demultiplexer_4_out0), .PixelOut(pixelmem_33_pixelout), .Draw(comparator_1_eq));
  pixelmem pixelmem_34 (
    .Data(rom_4_data), .Store(demultiplexer_4_out1), .PixelOut(pixelmem_34_pixelout), .Draw(comparator_1_eq));
  pixelmem pixelmem_35 (
    .Data(rom_4_data), .Store(demultiplexer_4_out2), .PixelOut(pixelmem_35_pixelout), .Draw(comparator_1_eq));
  pixelmem pixelmem_36 (
    .Data(rom_4_data), .Store(demultiplexer_4_out3), .PixelOut(pixelmem_36_pixelout), .Draw(comparator_1_eq));
  pixelmem pixelmem_37 (
    .Data(rom_4_data), .Store(demultiplexer_4_out4), .PixelOut(pixelmem_37_pixelout), .Draw(comparator_1_eq));
  pixelmem pixelmem_38 (
    .Data(rom_4_data), .Store(demultiplexer_4_out5), .PixelOut(pixelmem_38_pixelout), .Draw(comparator_1_eq));
  pixelmem pixelmem_39 (
    .Data(rom_4_data), .Store(demultiplexer_4_out6), .PixelOut(pixelmem_39_pixelout), .Draw(comparator_1_eq));
  pixelmem pixelmem_40 (
    .Data(rom_4_data), .Store(demultiplexer_4_out7), .PixelOut(pixelmem_40_pixelout), .Draw(comparator_1_eq));
  pixelmem pixelmem_41 (
    .Data(rom_4_data), .Store(demultiplexer_4_out8), .PixelOut(pixelmem_41_pixelout), .Draw(comparator_1_eq));
  pixelmem pixelmem_42 (
    .Data(rom_4_data), .Store(demultiplexer_4_out9), .PixelOut(pixelmem_42_pixelout), .Draw(comparator_1_eq));
  pixelmem pixelmem_43 (
    .Data(rom_4_data), .Store(demultiplexer_4_out10), .PixelOut(pixelmem_43_pixelout), .Draw(comparator_1_eq));
  pixelmem pixelmem_44 (
    .Data(rom_4_data), .Store(demultiplexer_4_out11), .PixelOut(pixelmem_44_pixelout), .Draw(comparator_1_eq));
  pixelmem pixelmem_45 (
    .Data(rom_4_data), .Store(demultiplexer_4_out12), .PixelOut(pixelmem_45_pixelout), .Draw(comparator_1_eq));
  pixelmem pixelmem_46 (
    .Data(rom_4_data), .Store(demultiplexer_4_out13), .PixelOut(pixelmem_46_pixelout), .Draw(comparator_1_eq));
  pixelmem pixelmem_47 (
    .Data(rom_4_data), .Store(demultiplexer_4_out14), .PixelOut(pixelmem_47_pixelout), .Draw(comparator_1_eq));
  pixelmem pixelmem_48 (
    .Data(rom_4_data), .Store(demultiplexer_4_out15), .PixelOut(pixelmem_48_pixelout), .Draw(comparator_1_eq));
  pixelmem pixelmem_49 (
    .Data(rom_4_data), .Store(demultiplexer_4_out16), .PixelOut(pixelmem_49_pixelout), .Draw(comparator_1_eq));
  pixelmem pixelmem_50 (
    .Data(rom_4_data), .Store(demultiplexer_4_out17), .PixelOut(pixelmem_50_pixelout), .Draw(comparator_1_eq));
  pixelmem pixelmem_51 (
    .Data(rom_4_data), .Store(demultiplexer_4_out18), .PixelOut(pixelmem_51_pixelout), .Draw(comparator_1_eq));
  pixelmem pixelmem_52 (
    .Data(rom_4_data), .Store(demultiplexer_4_out19), .PixelOut(pixelmem_52_pixelout), .Draw(comparator_1_eq));
  pixelmem pixelmem_53 (
    .Data(rom_4_data), .Store(demultiplexer_4_out20), .PixelOut(pixelmem_53_pixelout), .Draw(comparator_1_eq));
  pixelmem pixelmem_54 (
    .Data(rom_4_data), .Store(demultiplexer_4_out21), .PixelOut(pixelmem_54_pixelout), .Draw(comparator_1_eq));
  pixelmem pixelmem_55 (
    .Data(rom_4_data), .Store(demultiplexer_4_out22), .PixelOut(pixelmem_55_pixelout), .Draw(comparator_1_eq));
  pixelmem pixelmem_56 (
    .Data(rom_4_data), .Store(demultiplexer_4_out23), .PixelOut(pixelmem_56_pixelout), .Draw(comparator_1_eq));
  pixelmem pixelmem_57 (
    .Data(rom_4_data), .Store(demultiplexer_4_out24), .PixelOut(pixelmem_57_pixelout), .Draw(comparator_1_eq));
  pixelmem pixelmem_58 (
    .Data(rom_4_data), .Store(demultiplexer_4_out25), .PixelOut(pixelmem_58_pixelout), .Draw(comparator_1_eq));
  pixelmem pixelmem_59 (
    .Data(rom_4_data), .Store(demultiplexer_4_out26), .PixelOut(pixelmem_59_pixelout), .Draw(comparator_1_eq));
  pixelmem pixelmem_60 (
    .Data(rom_4_data), .Store(demultiplexer_4_out27), .PixelOut(pixelmem_60_pixelout), .Draw(comparator_1_eq));
  pixelmem pixelmem_61 (
    .Data(rom_4_data), .Store(demultiplexer_4_out28), .PixelOut(pixelmem_61_pixelout), .Draw(comparator_1_eq));
  pixelmem pixelmem_62 (
    .Data(rom_4_data), .Store(demultiplexer_4_out29), .PixelOut(pixelmem_62_pixelout), .Draw(comparator_1_eq));
  pixelmem pixelmem_63 (
    .Data(rom_4_data), .Store(demultiplexer_4_out30), .PixelOut(pixelmem_63_pixelout), .Draw(comparator_1_eq));
  pixelmem pixelmem_64 (
    .Data(rom_4_data), .Store(demultiplexer_4_out31), .PixelOut(pixelmem_64_pixelout), .Draw(comparator_1_eq));
  Demultiplexer #(.select(5)) demultiplexer_3 (
    .out0(demultiplexer_3_out0), .out1(demultiplexer_3_out1), .out2(demultiplexer_3_out2),
    .out3(demultiplexer_3_out3), .out4(demultiplexer_3_out4), .out5(demultiplexer_3_out5),
    .out6(demultiplexer_3_out6), .out7(demultiplexer_3_out7), .out8(demultiplexer_3_out8),
    .out9(demultiplexer_3_out9), .out10(demultiplexer_3_out10), .out11(demultiplexer_3_out11),
    .out12(demultiplexer_3_out12), .out13(demultiplexer_3_out13), .out14(demultiplexer_3_out14),
    .out15(demultiplexer_3_out15), .out16(demultiplexer_3_out16), .out17(demultiplexer_3_out17),
    .out18(demultiplexer_3_out18), .out19(demultiplexer_3_out19), .out20(demultiplexer_3_out20),
    .out21(demultiplexer_3_out21), .out22(demultiplexer_3_out22), .out23(demultiplexer_3_out23),
    .out24(demultiplexer_3_out24), .out25(demultiplexer_3_out25), .out26(demultiplexer_3_out26),
    .out27(demultiplexer_3_out27), .out28(demultiplexer_3_out28), .out29(demultiplexer_3_out29),
    .out30(demultiplexer_3_out30), .out31(demultiplexer_3_out31), .in(not_1_out), .sel(Row_q));  // open: en
  Demultiplexer #(.select(5)) demultiplexer_4 (
    .out0(demultiplexer_4_out0), .out1(demultiplexer_4_out1), .out2(demultiplexer_4_out2),
    .out3(demultiplexer_4_out3), .out4(demultiplexer_4_out4), .out5(demultiplexer_4_out5),
    .out6(demultiplexer_4_out6), .out7(demultiplexer_4_out7), .out8(demultiplexer_4_out8),
    .out9(demultiplexer_4_out9), .out10(demultiplexer_4_out10), .out11(demultiplexer_4_out11),
    .out12(demultiplexer_4_out12), .out13(demultiplexer_4_out13), .out14(demultiplexer_4_out14),
    .out15(demultiplexer_4_out15), .out16(demultiplexer_4_out16), .out17(demultiplexer_4_out17),
    .out18(demultiplexer_4_out18), .out19(demultiplexer_4_out19), .out20(demultiplexer_4_out20),
    .out21(demultiplexer_4_out21), .out22(demultiplexer_4_out22), .out23(demultiplexer_4_out23),
    .out24(demultiplexer_4_out24), .out25(demultiplexer_4_out25), .out26(demultiplexer_4_out26),
    .out27(demultiplexer_4_out27), .out28(demultiplexer_4_out28), .out29(demultiplexer_4_out29),
    .out30(demultiplexer_4_out30), .out31(demultiplexer_4_out31), .in(not_1_out), .sel(Row_q));  // open: en
  ROM #(.addrWidth(20), .dataWidth(32)) rom_3 (.addr(Address_q), .data(rom_3_data));  // open: sel
  ROM #(.addrWidth(20), .dataWidth(32)) rom_4 (.addr(Address_q), .data(rom_4_data));  // open: sel
endmodule

module pixelmem (
  input  [31:0] Data,
  input  Store,
  input  Draw,
  output [31:0] PixelOut
);

  wire [31:0] register_2_q;

  Register #(.width(32)) register_1 (.D(register_2_q), .Q(PixelOut), .clk(Draw));  // open: en, clr
  Register #(.width(32)) register_2 (.D(Data), .Q(register_2_q), .clk(Store));  // open: en, clr
endmodule

module pixelmem2 (
  input  [31:0] Data,
  input  Store,
  input  Draw,
  output [31:0] PixelOut
);

  wire [31:0] register_1_q;

  Register #(.width(32)) register_1 (.D(Data), .Q(register_1_q), .clk(Store));  // open: en, clr
  Register #(.width(32)) register_2 (.D(register_1_q), .Q(PixelOut), .clk(Draw));  // open: en, clr
endmodule
